# Fritzing sketch Esquematico (saved by Fritzing 1.0.4)
circuit board: 8.46667cm x 5.64444cm
breadboards: 1

parts:
  A1 = wt32-eth01
  S1 = Pushbutton [package="[THT]"]
  U2 = AVR 10-pin ICSP Header [package=avr_icsp]
  Part1 = FTDI Basic Programmer

nets:
  N1: A1.Pin_1, A1.Pin_4
  N2: A1.Pin_2, A1.Pin_9, A1.Pin_11, A1.Pin_14, A1.Pin_23, S1.Pin_3, S1.Pin_4, U2.10, Part1.GND
  N3: A1.Pin_3, A1.Pin_10, U2.1
  N4: A1.Pin_5, U2.7
  N5: A1.Pin_6, U2.9
  N6: A1.Pin_7, U2.8
  N7: A1.Pin_15, U2.4
  N8: A1.Pin_16, U2.3
  N9: A1.Pin_19, U2.6
  N10: A1.Pin_20, U2.5
  N11: A1.Pin_24, S1.Pin_1
  N12: A1.Pin_25, Part1.TXO
  N13: A1.Pin_26, Part1.RXI

notes:
  Alimentação: 3,3V

custom parts:
  wt32-eth01: WT32-ETH01 is an embedded serial port to Ethernet module based on ESP32 series designed by Wireless-Tag.
